# Fritzing sketch schematic (saved by Fritzing 0.9.4)

parts:
  J1 = Basic Servo
  MCU1 = Raspberry Pi Zero

nets:
  N1: J1.gnd, MCU1.pin_6, MCU1.pin_39
  N2: J1.vcc, MCU1.pin_4
  N3: J1.pulse, MCU1.pin_12
